# Fritzing sketch animal_button_box (saved by Fritzing 1.0.2b)
breadboards: 1

parts:
  Feather_RP2040 = Adafruit Feather RP2040 [part_number="Adafruit #4884"]
  IMU = Adafruit BNO055 STEMMA QT [part_number="Adafruit #4646"]
  E-Paper_Module = Waveshare 1.54in epaper display
  Battery = LIPO-110mAh [package=lipo-110]
  Buzzer = Piezo Speaker
  Arcade_Button = Round Pushbutton
  R1 = Resistor [tolerance=±5% resistance=100k package="2010 [SMD]"]
  R2 = Resistor [tolerance=±5% resistance=100k package="2010 [SMD]"]
  Update_Switch = Pushbutton [package=THT]

nets:
  GND: Feather_RP2040.GND, IMU.GND, E-Paper_Module.Pin_7, Battery.+, Buzzer.pin1, Arcade_Button.leg1, R1.Pin_1, Update_Switch.leg1
  +3V3: Feather_RP2040.+3V3, IMU.VCC, E-Paper_Module.Pin_8, Battery.-
  N1: Feather_RP2040.SDA, IMU.SDA
  N2: Feather_RP2040.SCL, IMU.SCL
  N3: Feather_RP2040.D4, Arcade_Button.leg0
  N4: Feather_RP2040.D24, Buzzer.pin2
  N5: Feather_RP2040.A2, IMU.INT_3V
  N6: Feather_RP2040.A1, Update_Switch.leg0
  N7: Feather_RP2040.A0, R1.Pin_0, R2.Pin_1
  N8: Feather_RP2040.VBAT, R2.Pin_0
  N9: Feather_RP2040.D13, E-Paper_Module.Pin_1
  N10: Feather_RP2040.D12, E-Paper_Module.Pin_2
  N11: Feather_RP2040.D11, E-Paper_Module.Pin_6
  N12: Feather_RP2040.D10, E-Paper_Module.Pin_5
  N13: Feather_RP2040.D9, E-Paper_Module.Pin_4
  N14: Feather_RP2040.D6, E-Paper_Module.Pin_3

custom parts:
  Adafruit Feather RP2040: A new chip means a new Feather, and the Raspberry Pi RP2040 is no exception. When we saw this chip we thought "this chip is going to be awesome when we give it the Feather Treatment" and so we did! This Feather features the RP2040, and all niceties you know and love about Feather Measures 2.0" x 0.9" x 0.28" (50.8mm x 22.8mm x 7mm) without headers soldered in Light as a (large?) feather - 5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
  Adafruit BNO055 STEMMA QT: If you've ever ordered and wire up a 9-DOF sensor, chances are you've also realized the challenge of turning the sensor data from an accelerometer, gyroscope, and magnetometer into actual "3D space orientation"! Orientation is a hard problem to solve. The sensor fusion algorithms (the secret sauce that blends accelerometer, magnetometer, and gyroscope data into stable three-axis orientation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
  Waveshare 1.54in epaper display: This is an E-Ink display module, 1.54inch, 200x200 resolution, with embedded controller, communicating via SPI interface.
